# Fritzing sketch m110-teensy (saved by Fritzing 0.9.3b)
circuit board: 5.64444cm x 8.46667cm
perfboards: 1

parts:
  MIDI_CONN = Buchsensteckerleiste - 4 pins [form="♀ (female)" package=THT]
  U7 = CD4504 [package=dil16]
  DISPLAY_CONN = Buchsensteckerleiste - 4 pins [form="♀ (female)" package=THT]
  D2 = Zener Diode [part_number=1N4732A breakdown_voltage=3.6V package="300 mil [THT]"]
  R1 = Resistor [tolerance=±5% resistance=10k package="1206 [SMD]"]
  Teensy_3_2 = Teensy 3.2
  D1 = Zener Diode [part_number=1N4732A breakdown_voltage=3.6V package="300 mil [THT]"]
  R2 = Resistor [tolerance=±5% resistance=10k package="1206 [SMD]"]
  U8 = M110-SOCKET-40 [package=dil40]
  C4 = Ceramic Capacitor [capacitance=100nF package="100 mil [THT, multilayer]"]
  C3 = Tantalum Capacitor [capacitance=1μF package="100 mil [THT, tantalum]"]
  Analog_Conn = Buchsensteckerleiste - 4 pins [form="♀ (female)" package=THT]

nets:
  N1: MIDI_CONN.pin1, Teensy_3_2.D0
  N2: MIDI_CONN.pin2, Teensy_3_2.D1
  GND: MIDI_CONN.pin_3, U7.GND, U7.TTLSEL, DISPLAY_CONN.pin_4, D2.anode, Teensy_3_2.GND, Teensy_3_2.AGND, D1.anode, U8.GND, C4.0, C3.-, Analog_Conn.pin_3
  5V/VCC: MIDI_CONN.pin_4, U7.VCC, DISPLAY_CONN.pin_3, Teensy_3_2.Vin, C4.1, Analog_Conn.pin_4
  N3: U7.1OUT, U8.2'
  N4: U7.1IN, Teensy_3_2.D30
  N5: U7.2OUT, U8.4'
  N6: U7.2IN, Teensy_3_2.D29
  N7: U7.3OUT, U8.8'
  N8: U7.3IN, Teensy_3_2.D28
  N9: U7.4IN, Teensy_3_2.D27
  N10: U7.4OUT, U8.16'
  N11: U7.5IN, Teensy_3_2.A8/D22
  N12: U7.5OUT, U8.TRIGGER
  N13: U7.6IN, Teensy_3_2.D6
  N14: U7.6OUT, U8.GATE
  12V: U7.VDD, U8.Vdd, C3.+, Analog_Conn.pin1
  N15: DISPLAY_CONN.pin1, Teensy_3_2.A5/D19
  N16: DISPLAY_CONN.pin2, Teensy_3_2.A4/D18
  N17: D2.cathode, R1.Pin_0, Teensy_3_2.D13
  N18: R1.Pin_1, U8.CLK_IN
  N19: Teensy_3_2.D2, U8.B2
  N20: Teensy_3_2.D3, U8.B3
  N21: Teensy_3_2.D4, U8.B4
  N22: Teensy_3_2.D5, U8.B5
  N23: Teensy_3_2.D7, U8.-F1
  N24: Teensy_3_2.D8, U8.-F2
  N25: Teensy_3_2.D9, U8.-F3
  N26: Teensy_3_2.D10, U8.-F4
  N27: Teensy_3_2.D11, U8.-F5
  N28: Teensy_3_2.D12, U8.-F6
  N29: Teensy_3_2.A0/D14, U8.-F7
  N30: Teensy_3_2.A1/D15, U8.-F8
  N31: Teensy_3_2.A2/D16, U8.-F9
  N32: Teensy_3_2.A3/D17, U8.-F10
  N33: Teensy_3_2.A6/D20, U8.-F11
  N34: Teensy_3_2.A7/D21, U8.-F12
  N35: Teensy_3_2.A9/D23, D1.cathode, R2.Pin_1
  N36: R2.Pin_0, U8.GLIDE

custom parts:
  Buchsensteckerleiste - 4 pins: Generic female header
  CD4504: Level shifter
  Teensy 3.2: The Teensy is a complete USB-based microcontoller development system, in a very small footprint, capable of implementing many types of projects. All programming is done via the USB port. No special programmer is needed, only a standard micro-USB cable and a PC or Macintosh with a USB port. It has a USB keyboard/mouse/joystick emulation stack and can be programmed through Arduino IDE.
  M110-SOCKET-40: 40-pin DIL socket meant to hold a Signetics M110 chip in the JEN SX-1000 synth
